# Fritzing sketch CTN-Montage-Diviseur (saved by Fritzing 0.9.2b)
breadboards: 1

parts:
  Composant1 = Arduino Uno (Rev3)
  R1 = Resistor [tolerance=±1% resistance=10k package=THT]
  R2 = Temperature Sensor (Thermistor) [thermistor_type=NTC package=THT]  # not connected

nets:
  N1: Composant1.A0, R1.Pin_1
  N2: Composant1.5V, R1.Pin_0
