# Fritzing sketch LED_CAN_Potentiometre (saved by Fritzing 0.9.2b)

parts:
  Composant1 = Arduino Uno (Rev3)
  R3 = Rotary Potentiometer (Small) [maximum_resistance=100kΩ package=THT]

nets:
  N1: Composant1.A0, R3.wiper
  N2: Composant1.5V, R3.leg2
  N3: Composant1.GND, R3.leg1
