# Fritzing sketch LED_PWM (saved by Fritzing 0.9.2b)

parts:
  Composant1 = Arduino Uno (Rev3)
  LED1 = LED - 5mm [color="Red (633nm)" package="5 mm [THT]"]
  R2 = Resistor [tolerance=±5% resistance=220 package=THT]

nets:
  N1: Composant1.D11_PWM/MOSI, R2.Pin_1
  N2: Composant1.GND, LED1.cathode
