# Fritzing sketch LED_PWM_Potentiometre (saved by Fritzing 0.9.2b)

parts:
  Composant1 = Arduino Uno (Rev3)
  LED1 = LED - 5mm [color="Red (633nm)" package="5 mm [THT]"]
  R2 = Resistor [tolerance=±5% resistance=220 package=THT]
  R3 = Rotary Potentiometer (Small) [maximum_resistance=100kΩ package=THT]

nets:
  N1: Composant1.A0, R3.wiper
  N2: Composant1.D11_PWM/MOSI, R2.Pin_1
  N3: Composant1.GND, LED1.cathode, R3.leg1
  N4: Composant1.5V, R3.leg2
