# Fritzing sketch Ultrason_HC-SR04_oscillo (saved by Fritzing 0.9.2b)

parts:
  Composant1 = Arduino Uno (Rev3)
  Composant2 = SRF05 Ultrasonic Rangefinder

nets:
  N1: Composant1.D8, Composant2.Trig
  N2: Composant1.D9_PWM, Composant2.Echo
  5V: Composant1.5V, Composant2.VCC
  GND: Composant1.GND, Composant2.GND

notes:
  CH1
  CH2
  CH3
  CH4
  Masse
