# Fritzing sketch ctn_montage_arduino (saved by Fritzing 0.9.4)

parts:
  Composant1 = Arduino Uno (Rev3)
  R1 = Resistor [tolerance=±1% resistance=10k package=THT]
  R2 = Temperature Sensor (Thermistor) [thermistor_type=NTC package=THT]

nets:
  N1: Composant1.5V, R1.Pin_0
  N2: Composant1.GND, R2.pin_0
  N3: R1.Pin_1, R2.pin_1

notes:
  CTN
  10k
