# Fritzing sketch ctn_montage_microbit (saved by Fritzing 0.9.4)

parts:
  R1 = Resistor [tolerance=±5% resistance=10k package=THT]
  R2 = Temperature Sensor (Thermistor) [thermistor_type=NTC package=THT]
  Mod1 = Microbit

nets:
  N1: R1.Pin_0, Mod1.3V3
  N2: R1.Pin_1, R2.pin_1
  N3: R2.pin_0, Mod1.GND

notes:
  CTN
  10k

custom parts:
  Microbit: BBC Microbit Fritzing part. May 2019 expanded to include schematic and pcb views as well as breadboard. PCB view assumes an Adafruit PRODUCT ID: 3342 2x40 Right Angle through hole edge connector (although others will probably work as well). The pcb svg is custom (see forum article http://forum.fritzing.org/t/making-edge-connectors-and-both-side-smd-parts/7287 for an explaination if you need to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
