# Fritzing sketch ctn_montage_pyboard (saved by Fritzing 0.9.4)

parts:
  Adafruit_Feather_STM32F1 = Adafruit Feather STM32F405 [part_number="Adafruit #4382"]
  R1 = Resistor [tolerance=±5% resistance=10k package=THT]
  R2 = Temperature Sensor (Thermistor) [thermistor_type=NTC package=THT]

nets:
  N1: Adafruit_Feather_STM32F1.GND, R2.pin_0
  N2: Adafruit_Feather_STM32F1.+3V3, R1.Pin_1
  N3: R1.Pin_0, R2.pin_1

notes:
  CTN
  10k
  Adafruit Feather STM32F405 Express

custom parts:
  Adafruit Feather STM32F405: The new STM32F405 Feather (video) that we designed runs CircuitPython at a blistering 168MHz – our fastest CircuitPython board ever! We put a STEMMA QT / Qwiic port on the end, so you can really easily plug and play I2C sensors. This Feather has lots of goodies: STM32F405 Cortex M4 with 1MB Flash, 168MHz speed 3.3V logic, but almost all pins are 5V compliant! USB C power and data - our first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
