# Fritzing sketch RC_constante_temps (saved by Fritzing 0.9.2b)
breadboards: 1

parts:
  Composant1 = Arduino Uno (Rev3)
  R1 = Resistor [tolerance=±5% resistance=1M package=THT]
  C1 = Ceramic Capacitor [capacitance=100nF package="100 mil [THT, multilayer]"]

nets:
  N1: Composant1.A0, R1.Pin_1, C1.0
  N2: Composant1.D8, R1.Pin_0
  N3: Composant1.GND, C1.1
